// Logisim project Single_Cylce_Processor.circ as structural Verilog: 12 circuits, main circuit main
module main (
);

  wire alu_1_zero, and_1_out, control_unit_1_alusrc, control_unit_1_branch, control_unit_1_memread,
       control_unit_1_memtoreg, control_unit_1_memwrite, control_unit_1_regwrite;
  wire [1:0] control_unit_1_aluop;
  wire [3:0] alu_control_1_out_3;
  wire [31:0] add_1_out_3, add_2_out_3, alu_1_alu_result, data_mem_1_read_data, imm_gen_1_out_2,
       inst_mem_1_instruction, mux_1_out_4, mux_2_out_4, mux_3_out_4, pc_1_out_2, reg_file_1_read_data_1,
       reg_file_1_read_data_2, shift_1_1_out_2;

  PC pc_1 (.in_1(mux_2_out_4), .out_2(pc_1_out_2));
  Inst_mem inst_mem_1 (.Read_address(pc_1_out_2), .Instruction(inst_mem_1_instruction));
  Add add_1 (.in_1(pc_1_out_2), .in_2(32'h4), .out_3(add_1_out_3));
  Imm_Gen imm_gen_1 (.in_1(pc_1_out_2), .out_2(imm_gen_1_out_2));
  Control_Unit control_unit_1 (
    .in_1(inst_mem_1_instruction[6:0]), .Branch(control_unit_1_branch), .MemRead(control_unit_1_memread),
    .MemtoReg(control_unit_1_memtoreg), .ALUOp(control_unit_1_aluop), .MemWrite(control_unit_1_memwrite),
    .ALUSrc(control_unit_1_alusrc), .RegWrite(control_unit_1_regwrite));
  Reg_File reg_file_1 (
    .RegWrite(control_unit_1_regwrite), .Read_register_1(inst_mem_1_instruction[19:15]),
    .Read_register_2(inst_mem_1_instruction[24:20]), .Write_register(inst_mem_1_instruction[11:7]),
    .Write_data(mux_3_out_4), .Read_data_1(reg_file_1_read_data_1), .Read_data_2(reg_file_1_read_data_2));
  ALU_Control alu_control_1 (
    .in_1({inst_mem_1_instruction[30], inst_mem_1_instruction[14:12]}), .in_2(control_unit_1_aluop),
    .out_3(alu_control_1_out_3));
  Shift_1 shift_1_1 (.in_1(imm_gen_1_out_2), .out_2(shift_1_1_out_2));
  MUX mux_1 (
    .choice_0(reg_file_1_read_data_2), .choice_1(imm_gen_1_out_2), .S(control_unit_1_alusrc),
    .out_4(mux_1_out_4));
  Add add_2 (.in_1(pc_1_out_2), .in_2(shift_1_1_out_2), .out_3(add_2_out_3));
  and and_1 (and_1_out, control_unit_1_branch, alu_1_zero);
  ALU alu_1 (
    .in_1(reg_file_1_read_data_1), .in_2(mux_1_out_4), .in_3(alu_control_1_out_3), .Zero(alu_1_zero),
    .ALU_result(alu_1_alu_result));
  MUX mux_2 (.choice_0(add_1_out_3), .choice_1(add_2_out_3), .S(and_1_out), .out_4(mux_2_out_4));
  Data_mem data_mem_1 (
    .MemWrite(control_unit_1_memwrite), .Address(alu_1_alu_result), .Write_data(reg_file_1_read_data_2),
    .MemRead(control_unit_1_memread), .Read_data(data_mem_1_read_data));
  MUX mux_3 (
    .choice_0(alu_1_alu_result), .choice_1(data_mem_1_read_data), .S(control_unit_1_memtoreg),
    .out_4(mux_3_out_4));
endmodule

module PC (
  input  [31:0] in_1,
  output [31:0] out_2
);
endmodule

module Add (
  input  [31:0] in_1,
  input  [31:0] in_2,
  output [31:0] out_3
);
endmodule

module Inst_mem (
  input  [31:0] Read_address,
  output [31:0] Instruction
);
endmodule

module Imm_Gen (
  input  [31:0] in_1,
  output [31:0] out_2
);
endmodule

module Reg_File (
  input  RegWrite,
  input  [4:0] Read_register_1,
  input  [4:0] Read_register_2,
  input  [4:0] Write_register,
  input  [31:0] Write_data,
  output [31:0] Read_data_1,
  output [31:0] Read_data_2
);
endmodule

module Control_Unit (
  input  [6:0] in_1,
  output Branch,
  output MemRead,
  output MemtoReg,
  output [1:0] ALUOp,
  output MemWrite,
  output ALUSrc,
  output RegWrite
);
endmodule

module Shift_1 (
  input  [31:0] in_1,
  output [31:0] out_2
);
endmodule

module MUX (
  input  [31:0] choice_0,
  input  [31:0] choice_1,
  input  S,
  output [31:0] out_4
);
endmodule

module ALU (
  input  [31:0] in_1,
  input  [31:0] in_2,
  input  [3:0] in_3,
  output Zero,
  output [31:0] ALU_result
);
endmodule

module Data_mem (
  input  MemWrite,
  input  [31:0] Address,
  input  [31:0] Write_data,
  input  MemRead,
  output [31:0] Read_data
);
endmodule

module ALU_Control (
  input  [3:0] in_1,
  input  [1:0] in_2,
  output [3:0] out_3
);
endmodule
