// Logisim project temp.circ as structural Verilog: 4 circuits, main circuit Processor
module Processor (
);

  wire control_unit_1_memread, control_unit_1_memwrite, control_unit_1_regwrite;
  wire [1:0] control_unit_1_aluop;
  wire [3:0] alu_control_unit_1_alusel;
  wire [31:0] datapath_1_inst;

  Control_Unit control_unit_1 (
    .Inst(datapath_1_inst), .MemRead(control_unit_1_memread), .MemWrite(control_unit_1_memwrite),
    .RegWrite(control_unit_1_regwrite), .ALUOp(control_unit_1_aluop));
  ALU_Control_Unit alu_control_unit_1 (.ALUOp(control_unit_1_aluop), .ALUSel(alu_control_unit_1_alusel));
  Datapath datapath_1 (
    .MemRead(control_unit_1_memread), .MemWrite(control_unit_1_memwrite), .RegWrite(control_unit_1_regwrite),
    .ALUSel(alu_control_unit_1_alusel), .Inst(datapath_1_inst));
endmodule

module Datapath (
  input  MemRead,
  input  MemWrite,
  input  RegWrite,
  input  [3:0] ALUSel,
  output [31:0] Inst
);
endmodule

module Control_Unit (
  input  [31:0] Inst,
  output MemRead,
  output MemWrite,
  output RegWrite,
  output [1:0] ALUOp
);
endmodule

module ALU_Control_Unit (
  input  [1:0] ALUOp,
  output [3:0] ALUSel
);
endmodule
